// Logisim project RISC-V Multicycle Control Unit.circ as structural Verilog: 1 circuit, main circuit main
// PCSource
module main (
  input  [6:0] in_1,
  input  enable,
  input  clock,
  input  in_4,
  output PCWrite,
  output PCWriteCond,
  output IorD,
  output MemRead,
  output MemWrite,
  output IRWrite,
  output PCSource,
  output SrcReg,
  output ALUOp1,
  output ALUOp0,
  output ALUSrcB1,
  output ALUSrcB0,
  output ALUSrcA,
  output RegWrite
);

  wire _0__1_out, _1__2_out, _1__4_out, _1__8_out, _1__9_out, _2__3_out, _3__0_out, _4__5_out, _4__7_out,
       _5__6_out, _6__0_out, _7__0_out, _8__0_out, not_1_out, not_2_out, not_3_out, not_4_out, not_5_out,
       not_6_out, not_7_out, not_8_out, not_9_out, not_10_out, not_11_out, or_1_out;
  wire [3:0] or_5_out, register_1_q;

  not not_1 (not_1_out, in_1[0]);
  not not_2 (not_2_out, in_1[1]);
  not not_3 (not_3_out, in_1[2]);
  not not_4 (not_4_out, in_1[3]);
  not not_5 (not_5_out, in_1[4]);
  not not_6 (not_6_out, in_1[5]);
  not not_7 (not_7_out, in_1[6]);
  not not_8 (not_8_out, register_1_q[0]);
  not not_9 (not_9_out, register_1_q[1]);
  not not_10 (not_10_out, register_1_q[2]);
  not not_11 (not_11_out, register_1_q[3]);
  and _0__1 (_0__1_out, not_8_out, not_9_out, not_10_out, not_11_out);
  and _1__2 (_1__2_out, not_7_out, in_1[5], in_1[4], not_4_out, not_3_out, in_1[1], in_1[0], not_11_out, not_10_out, not_9_out, register_1_q[0]);
  or or_1 (or_1_out, not_6_out, in_1[5]);
  and _1__4 (_1__4_out, not_7_out, or_1_out, not_5_out, not_4_out, not_3_out, in_1[1], in_1[0], not_11_out, not_10_out, not_9_out, register_1_q[0]);
  and _1__8 (_1__8_out, in_1[6], in_1[5], not_5_out, not_4_out, not_3_out, in_1[1], in_1[0], not_11_out, not_10_out, not_9_out, register_1_q[0]);
  and _1__9 (_1__9_out, in_1[6], in_1[5], not_5_out, in_1[3], in_1[2], in_1[1], in_1[0], not_11_out, not_10_out, not_9_out, register_1_q[0]);
  and _2__3 (_2__3_out, not_11_out, not_10_out, register_1_q[1], not_8_out);
  and _3__0 (_3__0_out, not_11_out, not_10_out, register_1_q[1], register_1_q[0]);
  and _4__5 (_4__5_out, not_6_out, not_11_out, register_1_q[2], not_9_out, register_1_q[0]);
  and _4__7 (_4__7_out, in_1[5], not_11_out, register_1_q[2], register_1_q[1], register_1_q[0]);
  and _5__6 (_5__6_out, not_11_out, register_1_q[2], not_9_out, register_1_q[0]);
  and _6__0 (_6__0_out, not_11_out, register_1_q[2], register_1_q[1], not_8_out);
  and _7__0 (_7__0_out, register_1_q[2], register_1_q[1], register_1_q[0]);
  and _8__0 (_8__0_out, register_1_q[3], not_10_out, not_9_out, not_8_out);
  or or_2 (or_5_out[3], _1__9_out, _1__8_out);
  or or_3 (or_5_out[2], _5__6_out, _4__7_out, _4__5_out, _1__4_out);
  or or_4 (or_5_out[1], _5__6_out, _4__7_out, _2__3_out, _1__2_out);
  or or_5 (or_5_out[0], _4__7_out, _4__5_out, _2__3_out, _1__9_out, _0__1_out);
  Register #(.width(4)) register_1 (.D(or_5_out), .en(enable), .Q(register_1_q), .clk(clock), .clr(in_4));
  or or_6 (PCWrite, _0__1_out, _1__9_out);
  buf or_7 (PCWriteCond, _1__8_out);  // OR_Gate
  or or_8 (IorD, _4__5_out, _4__7_out);
  or or_9 (MemRead, _8__0_out, _7__0_out, _6__0_out, _3__0_out, _4__5_out);
  buf or_10 (MemWrite, _4__7_out);  // OR_Gate
  or or_11 (IRWrite, _8__0_out, _7__0_out, _6__0_out, _3__0_out);
  or or_12 (PCSource, _0__1_out, _1__8_out, _1__9_out);
  buf or_13 (SrcReg, _1__9_out);  // OR_Gate
  buf or_14 (ALUOp1, _1__2_out);  // OR_Gate
  buf or_15 (ALUOp0, _1__8_out);  // OR_Gate
  or or_16 (ALUSrcB1, _0__1_out, _1__4_out);
  or or_17 (ALUSrcB0, _8__0_out, _7__0_out, _6__0_out, _3__0_out, _0__1_out);
  or or_18 (ALUSrcA, _1__2_out, _1__4_out, _1__8_out);
  or or_19 (RegWrite, _1__9_out, _2__3_out, _5__6_out);

  // Notes on the sheet:
  //   op0
  //   op1
  //   op2
  //   op3
  //   op4
  //   op5
  //   op6
  //   in0
  //   in1
  //   in2
  //   in3
endmodule
